# Fritzing sketch Barn-Door-Tracker-AccelStepper (saved by Fritzing 0.9.3b)

parts:
  Part1 = Arduino Nano (Rev3.0)
  MOTOR1 = 28BYJ-48 Stepper Motor
  X2 = X113647 Stepper Driver Board [part_number=X113647 package=board]
  S1 = Momentary Switch [package=ksa_sealed_tac_switch]
  5vdc_0_5A_from_USB_backup_battery = USB TTL Serial Cable

nets:
  N1: Part1.D3, X2.IN1
  N2: Part1.D4, X2.IN2
  N3: Part1.D5, X2.IN3
  N4: Part1.D6, X2.IN4
  VIN: Part1.VIN, X2.+V, 5vdc_0_5A_from_USB_backup_battery.5V
  GND: Part1.GND, X2.GND, S1.4, 5vdc_0_5A_from_USB_backup_battery.GND
  N5: Part1.A1, S1.2
  N6: MOTOR1.RED, X2.RED
  N7: MOTOR1.ORANGE, X2.ORANGE
  N8: MOTOR1.YELLOW, X2.YELLOW
  N9: MOTOR1.PINK, X2.PINK
  N10: MOTOR1.BLUE, X2.BLUE

notes:
  D3 <--> IN1
  D4 <--> IN2
  D5 <--> IN3
  D6 <--> IN4
  5v DC 0.5 - 1.0 A
  From USB Backup 'brick'

custom parts:
  X113647 Stepper Driver Board: A common stepper motor driver board based on ULN2003APG darlington array
