# Fritzing sketch 2x-gy-521-MPU6050-schematic (saved by Fritzing 0.9.3b)
breadboards: 1

parts:
  GY1 = MPU-6050 Board GY-521 [form="♀ (female)" package=THT]
  GY2 = MPU-6050 Board GY-521 [form="♀ (female)" package=THT]
  Part1 = Arduino Uno (Rev3)

nets:
  VCC: GY1.VCC, GY2.VCC, Part1.5V
  GND: GY1.GND, GY2.GND, GY2.pin7
  N1: GY1.pin3, GY2.pin3, Part1.A5/SCL
  N2: GY1.pin4, GY2.pin4, Part1.A4/SDA
  N3: GY1.pin7, Part1.3V3
  N4: GY1.pin8, Part1.D3_PWM
  N5: GY2.pin8, Part1.D2

notes:
  Notes:
  a) Arduino incoming power via USB not shown.
  b) One MPU is fixed to the body, the other is dynamic and attached to the head for tracking. The code will eventually calculate the diff between the head and body to determine the relative yaw and pitch of the shoulder cannon.

custom parts:
  MPU-6050 Board GY-521: Acelerometro y Giroscopio MPU-6050 Board GY-521
