# Fritzing sketch ardu-predator-schematic (saved by Fritzing 0.9.3b)
breadboards: 1

parts:
  J1 = Basic Servo
  J2 = Basic Servo
  MPU6050 = MPU-6050 Board GY-521 [form="♀ (female)" package=THT]
  Pull_Up_Resistors = Resistor [tolerance=±5% resistance=10k package=THT]
  R2 = Resistor [tolerance=±5% resistance=10k package=THT]
  Part2 = Arduino Uno (Rev3)
  5vdc_-_2A = 4 x AAA Battery Mount
  C4 = Capacitor Polarized [package=cpol-radial-100uf-25v]
  100uf_@_25v = Capacitor Polarized [package=cpol-radial-100uf-25v]

nets:
  GND: J1.gnd, J2.gnd, MPU6050.GND, MPU6050.pin7, Part2.GND, 5vdc_-_2A.-, C4.+, 100uf_@_25v.+
  VCC: J1.vcc, J2.vcc, 5vdc_-_2A.+, C4.-, 100uf_@_25v.-
  N1: J1.pulse, Part2.D9_PWM
  N2: J2.pulse, Part2.D10_PWM/SS
  VCC_2: MPU6050.VCC, Pull_Up_Resistors.Pin_0, R2.Pin_0, Part2.5V
  N3: MPU6050.pin3, R2.Pin_1, Part2.A5/SCL
  N4: MPU6050.pin4, Pull_Up_Resistors.Pin_1, Part2.A4/SDA
  N5: MPU6050.pin8, Part2.D2

notes:
  Notes:
  a) Arduino incoming power via USB not shown.
  b) The ground of the external servo power supply must be tied to the arduino ground.

custom parts:
  MPU-6050 Board GY-521: Acelerometro y Giroscopio MPU-6050 Board GY-521
